// Logisim project input.circ as structural Verilog: 5 circuits, main circuit main
// Runway Status
module main (
  input  [2:0] in_1
);

  wire Runway_status_runway_a_status, Runway_status_runway_b_status, Runway_status_wait_signal;
  wire [2:1] d_ff_2_q;
  wire [3:0] Runway_Picker_o4_o3_o2_o1;

  runway_picker Runway_Picker (.D1_D2_A_B_En({in_1[2:1], d_ff_2_q, in_1[0]}), .O4_O3_O2_O1(Runway_Picker_o4_o3_o2_o1));
  LED Wait_For_Landing (.in(Runway_status_wait_signal));
  D_Flip_Flop d_ff_1 (
    .clk(in_1[0]), .D(Runway_status_runway_a_status), .Q(d_ff_2_q[2]));  // open: Qn, preset, en, reset
  D_Flip_Flop d_ff_2 (
    .clk(in_1[0]), .D(Runway_status_runway_b_status), .Q(d_ff_2_q[1]));  // open: Qn, preset, en, reset
  LED led_1 (.in(Runway_status_runway_a_status));
  LED led_2 (.in(Runway_status_runway_b_status));
  runway_status Runway_status (
    .Runway_B_Status(Runway_status_runway_b_status), .Runway_A_Status(Runway_status_runway_a_status),
    .Wait_signal(Runway_status_wait_signal), .Bit_0_is_enable({Runway_Picker_o4_o3_o2_o1, in_1[0]}));
endmodule

module runway_picker (
  input  [4:0] D1_D2_A_B_En,
  output [3:0] O4_O3_O2_O1
);

  wire and_1_out, and_2_out, not_1_out, not_2_out, not_3_out, or_1_out;

  and and_1 (and_1_out, D1_D2_A_B_En[1], D1_D2_A_B_En[2]);
  not not_1 (not_1_out, D1_D2_A_B_En[1]);
  not not_2 (not_2_out, D1_D2_A_B_En[3]);
  and and_2 (and_2_out, not_1_out, not_2_out);
  not not_3 (not_3_out, and_1_out);
  or or_1 (or_1_out, D1_D2_A_B_En[2], and_2_out);
  and and_3 (O4_O3_O2_O1[3], D1_D2_A_B_En[0], 1'b1);
  and and_4 (O4_O3_O2_O1[2], D1_D2_A_B_En[0], and_1_out);
  and and_5 (O4_O3_O2_O1[1], D1_D2_A_B_En[0], not_3_out);
  and and_6 (O4_O3_O2_O1[0], D1_D2_A_B_En[0], or_1_out);

  // Notes on the sheet:
  //   Runway Picker
  //   O4 = 1
  //   O3 = A.B
  //   O2 = (A.B)'
  //   O1 = A + B'.D2'
endmodule

module runway_status (
  input  [4:0] Bit_0_is_enable,
  output Runway_B_Status,
  output Runway_A_Status,
  output Wait_signal
);

  wire _4_16_Decoder__10, _4_16_Decoder__11, clock_1_out, clock_2_out,
       Counter_2_carry_is_1_when_counter_finishes, Counter_carry_is_1_when_counter_finishes, not_1_out,
       not_2_out, not_3_out, not_4_out, s_r_ff_1_q, s_r_ff_2_q;

  decoder _4_16_Decoder (
    .A__LSB(Bit_0_is_enable[1]), .B(Bit_0_is_enable[2]), .C(Bit_0_is_enable[3]), .D__MSB(Bit_0_is_enable[4]),
    .Enable(Bit_0_is_enable[0]), ._10(_4_16_Decoder__10), ._11(_4_16_Decoder__11), ._13(Wait_signal));  // open: _0, _1, _2, _3, _4, _5, _6, _7, _8, _9, _12, _14, _15
  Clock clock_1 (.out(clock_1_out));
  and and_1 (Runway_A_Status, not_1_out, s_r_ff_1_q);
  counter Counter (
    .Carry_is_1_when_counter_finishes(Counter_carry_is_1_when_counter_finishes), .Clock(clock_1_out),
    .Reset(not_2_out));
  not not_1 (not_1_out, Counter_carry_is_1_when_counter_finishes);
  S_R_Flip_Flop s_r_ff_1 (
    .S(_4_16_Decoder__10), .clk(clock_1_out), .R(1'b0), .Q(s_r_ff_1_q),
    .reset(Counter_carry_is_1_when_counter_finishes));  // open: Qn, preset, en
  not not_2 (not_2_out, s_r_ff_1_q);
  Clock clock_2 (.out(clock_2_out));
  and and_2 (Runway_B_Status, not_4_out, s_r_ff_2_q);
  S_R_Flip_Flop s_r_ff_2 (
    .S(_4_16_Decoder__11), .clk(clock_2_out), .R(1'b0), .Q(s_r_ff_2_q),
    .reset(Counter_2_carry_is_1_when_counter_finishes));  // open: Qn, preset, en
  counter Counter_2 (
    .Carry_is_1_when_counter_finishes(Counter_2_carry_is_1_when_counter_finishes), .Clock(clock_2_out),
    .Reset(not_3_out));
  not not_3 (not_3_out, s_r_ff_2_q);
  not not_4 (not_4_out, Counter_2_carry_is_1_when_counter_finishes);

  // Notes on the sheet:
  //   Bit 1-4 is the output from runway picker
  //   a
  //   b
  //   d
endmodule

module decoder (
  input  A__LSB,
  input  B,
  input  C,
  input  D__MSB,
  input  Enable,
  output _0,
  output _1,
  output _2,
  output _3,
  output _4,
  output _5,
  output _6,
  output _7,
  output _8,
  output _9,
  output _10,
  output _11,
  output _12,
  output _13,
  output _14,
  output _15
);

  wire not_1_out, not_2_out, not_3_out, not_4_out;

  not not_1 (not_1_out, A__LSB);
  not not_2 (not_2_out, B);
  not not_3 (not_3_out, C);
  not not_4 (not_4_out, D__MSB);
  and and_1 (_0, Enable, not_4_out, not_3_out, not_2_out, not_1_out);
  and and_2 (_1, Enable, not_4_out, not_3_out, not_2_out, A__LSB);
  and and_3 (_2, Enable, not_4_out, not_3_out, B, not_1_out);
  and and_4 (_3, Enable, not_4_out, not_3_out, B, A__LSB);
  and and_5 (_4, Enable, not_4_out, C, not_2_out, not_1_out);
  and and_6 (_6, Enable, not_4_out, C, B, not_1_out);
  and and_7 (_5, Enable, not_4_out, C, not_2_out, A__LSB);
  and and_8 (_7, Enable, not_4_out, C, B, A__LSB);
  and and_9 (_9, Enable, D__MSB, not_3_out, not_2_out, A__LSB);
  and and_10 (_8, Enable, D__MSB, not_3_out, not_2_out, not_1_out);
  and and_11 (_10, Enable, D__MSB, not_3_out, B, not_1_out);
  and and_12 (_11, Enable, D__MSB, not_3_out, B, A__LSB);
  and and_13 (_12, Enable, D__MSB, C, not_2_out, not_1_out);
  and and_14 (_13, Enable, D__MSB, C, not_2_out, A__LSB);
  and and_15 (_14, Enable, D__MSB, C, B, not_1_out);
  and and_16 (_15, Enable, D__MSB, C, B, A__LSB);

  // Notes on the sheet:
  //   4:16 Decoder
endmodule

module counter (
  input  Clock,
  input  Reset,
  output Carry_is_1_when_counter_finishes
);

  wire and_1_out, not_1_out;
  wire [3:0] t_ff_1_q;

  and and_1 (and_1_out, not_1_out, Clock);
  not not_1 (not_1_out, Carry_is_1_when_counter_finishes);
  T_Flip_Flop t_ff_1 (.clk(and_1_out), .T(1'b1), .Q(t_ff_1_q[0]), .reset(Reset), .en(1'b1));  // open: Qn, preset
  and and_2 (Carry_is_1_when_counter_finishes, t_ff_1_q[3], t_ff_1_q[2]);
  T_Flip_Flop #(.trigger("falling")) t_ff_2 (
    .clk(t_ff_1_q[0]), .T(1'b1), .Q(t_ff_1_q[1]), .reset(Reset), .en(1'b1));  // open: Qn, preset
  T_Flip_Flop #(.trigger("falling")) t_ff_3 (
    .clk(t_ff_1_q[1]), .T(1'b1), .Q(t_ff_1_q[2]), .reset(Reset), .en(1'b1));  // open: Qn, preset
  // Probe on t_ff_1_q
  T_Flip_Flop #(.trigger("falling")) t_ff_4 (
    .clk(t_ff_1_q[2]), .T(1'b1), .Q(t_ff_1_q[3]), .reset(Reset), .en(1'b1));  // open: Qn, preset

  // Notes on the sheet:
  //   4 bit up counter
endmodule
