// Logisim project runway_picker.circ as structural Verilog: 1 circuit, main circuit main
module main (
  input  Direction_1,
  input  Direction_2,
  input  Runway_A_status,
  input  Runway_B_status,
  output out_5,
  output out_6
);

  wire and_2_out, and_3_out, not_1_out, not_2_out, not_3_out;

  not not_1 (not_1_out, Runway_A_status);
  not not_2 (not_2_out, Runway_B_status);
  not not_3 (not_3_out, Direction_2);
  and and_1 (out_5, Runway_A_status, Runway_B_status);
  and and_2 (and_2_out, Runway_A_status, not_2_out);
  and and_3 (and_3_out, not_3_out, not_1_out, not_2_out);
  or or_1 (out_6, and_2_out, and_3_out);
endmodule
