// Logisim project input.circ as structural Verilog: 1 circuit, main circuit main
module main (
  input  [1:0] Direction
);

  wire clock_1_out;
  wire [1:0] register_1_q, register_2_q, Runway_Picker_out_6, Runway_status_runway_b_status;
  wire [3:0] register_3_q;

  Button button_1 (.out(register_3_q[2]));
  Button button_2 (.out(register_3_q[3]));
  Register #(.width(2)) register_1 (.D(Direction), .Q(register_1_q), .clk(clock_1_out));  // open: en, clr
  runway_picker_main Runway_Picker (
    .Direction_1(register_1_q[0]), .Direction_2(register_1_q[1]), .Runway_A_status(register_2_q[0]),
    .Runway_B_status(register_2_q[1]), .out_5(Runway_Picker_out_6[1]), .out_6(Runway_Picker_out_6[0]));
  runway_status_main Runway_status (
    .Runway_B_status(Runway_status_runway_b_status[0]), .Runway_A_status(Runway_status_runway_b_status[1]),
    .in_1(register_3_q));
  Register #(.width(2)) register_2 (
    .D(Runway_status_runway_b_status), .Q(register_2_q), .clk(clock_1_out));  // open: en, clr
  Register #(.width(2)) register_3 (
    .D(Runway_Picker_out_6), .Q(register_3_q[1:0]), .clk(clock_1_out));  // open: en, clr
  Clock clock_1 (.out(clock_1_out));
endmodule
