// Logisim project runway_status.circ as structural Verilog: 1 circuit, main circuit main
module main (
  input  [1:0] Chosen_Runway,
  output Runway_B_status,
  output Runway_A_status
);

  wire button_1_out, button_2_out, clock_1_out, counter_1_carry, counter_2_carry, demultiplexer_1_out0,
       demultiplexer_1_out1, not_1_out, not_2_out, not_3_out, not_4_out, s_r_ff_1_q, s_r_ff_2_q;

  Demultiplexer #(.select(2)) demultiplexer_1 (
    .out0(demultiplexer_1_out0), .out1(demultiplexer_1_out1), .in(1'b1), .sel(Chosen_Runway));  // open: out2, out3, en
  Button button_1 (.out(button_1_out));
  Clock clock_1 (.out(clock_1_out));
  and and_1 (Runway_A_status, s_r_ff_1_q, not_2_out);
  Counter #(.width(4), .max('hd), .ongoal("stay")) counter_1 (
    .carry(counter_1_carry), .clk(clock_1_out), .clr(not_1_out));  // open: load, D, count, Q
  not not_1 (not_1_out, s_r_ff_1_q);
  and and_2 (Runway_B_status, s_r_ff_2_q, not_4_out);
  S_R_Flip_Flop s_r_ff_1 (
    .S(demultiplexer_1_out0), .clk(clock_1_out), .R(button_1_out), .Q(s_r_ff_1_q), .reset(button_1_out));  // open: Qn, preset, en
  not not_2 (not_2_out, counter_1_carry);
  Counter #(.width(4), .max('hd), .ongoal("stay")) counter_2 (
    .carry(counter_2_carry), .clk(clock_1_out), .clr(not_3_out));  // open: load, D, count, Q
  not not_3 (not_3_out, s_r_ff_2_q);
  S_R_Flip_Flop s_r_ff_2 (
    .S(demultiplexer_1_out1), .clk(clock_1_out), .R(button_2_out), .Q(s_r_ff_2_q), .reset(button_2_out));  // open: Qn, preset, en
  not not_4 (not_4_out, counter_2_carry);
  Button button_2 (.out(button_2_out));

  // Notes on the sheet:
  //   00 for A, 01 for B, 11 for reset
endmodule
